// Logisim project t24.circ as structural Verilog: 3 circuits, main circuit main
module main (
  input  in_1,
  input  in_2,
  input  in_3,
  input  in_4,
  input  in_5
);

  wire button_1_out, clock_1_out, clock_2_out, clock_3_out, d_1_q1, d_ff_1_q, multiplexer_1_out,
       multiplexer_2_out;
  wire [3:0] t_ff_1_q;

  Clock clock_1 (.out(clock_1_out));
  Button button_1 (.out(button_1_out));
  Multiplexer multiplexer_1 (.in0(d_ff_1_q), .in1(in_2), .out(multiplexer_1_out), .sel(in_4));  // open: en
  // NAND_Gate nand_1 has open pins: in0=in_1, in1=in_1, out=open
  Clock clock_2 (.out(clock_2_out));
  D_Flip_Flop d_ff_1 (.clk(clock_2_out), .D(multiplexer_1_out), .Q(d_ff_1_q));  // open: Qn, preset, en, reset
  T_Flip_Flop t_ff_1 (.clk(clock_1_out), .T(in_1), .Q(t_ff_1_q[0]), .preset(button_1_out));  // open: Qn, reset, en
  T_Flip_Flop t_ff_2 (.clk(t_ff_1_q[0]), .T(in_1), .Q(t_ff_1_q[1]), .preset(button_1_out));  // open: Qn, reset, en
  T_Flip_Flop t_ff_3 (.clk(t_ff_1_q[1]), .T(in_1), .Q(t_ff_1_q[2]), .preset(button_1_out));  // open: Qn, reset, en
  T_Flip_Flop t_ff_4 (.clk(t_ff_1_q[2]), .T(in_1), .Q(t_ff_1_q[3]), .preset(button_1_out));  // open: Qn, reset, en
  Multiplexer multiplexer_2 (.in0(d_1_q1), .in1(in_3), .out(multiplexer_2_out), .sel(in_5));  // open: en
  Clock clock_3 (.out(clock_3_out));
  D d_1 (.entreada(clock_3_out), .clock(multiplexer_2_out), .q1(d_1_q1));  // open: q2
  Hex_Digit_Display hex_digit_display_1 (.value(t_ff_1_q));  // open: dp
endmodule

module D (
  input  entreada,
  input  clock,
  output q1,
  output q2
);

  wire nand_1_out, nand_2_out, undriven;

  nand nand_1 (nand_1_out, entreada, undriven);
  nand nand_2 (nand_2_out, nand_1_out, clock);
  nand nand_3 (q1, nand_1_out, q2);
  nand nand_4 (q2, q1, nand_2_out);
endmodule

module Reg_8bits (
  input  in_1,
  input  [7:0] in_2,
  output [7:0] out_3
);

  D_Flip_Flop d_ff_1 (.clk(in_1), .D(in_2[7]), .Q(out_3[7]));  // open: Qn, preset, en, reset
  D_Flip_Flop d_ff_2 (.clk(in_1), .D(in_2[6]), .Q(out_3[6]));  // open: Qn, preset, en, reset
  D_Flip_Flop d_ff_3 (.clk(in_1), .D(in_2[5]), .Q(out_3[5]));  // open: Qn, preset, en, reset
  D_Flip_Flop d_ff_4 (.clk(in_1), .D(in_2[4]), .Q(out_3[4]));  // open: Qn, preset, en, reset
  D_Flip_Flop d_ff_5 (.clk(in_1), .D(in_2[3]), .Q(out_3[3]));  // open: Qn, preset, en, reset
  D_Flip_Flop d_ff_6 (.clk(in_1), .D(in_2[2]), .Q(out_3[2]));  // open: Qn, preset, en, reset
  D_Flip_Flop d_ff_7 (.clk(in_1), .D(in_2[1]), .Q(out_3[1]));  // open: Qn, preset, en, reset
  D_Flip_Flop d_ff_8 (.clk(in_1), .D(in_2[0]), .Q(out_3[0]));  // open: Qn, preset, en, reset
endmodule
